# Fritzing sketch wiringidagram (saved by Fritzing 0.7.10b)
breadboards: 1

parts:
  R1 = Rotary Potentiometer (Small) [maximum_resistance=100kΩ]  # not connected
  Arduino1 = Arduino
  LED1 = LED - 5mm [color="Green (555nm)" package="5 mm [THT]"]
  LED2 = LED - 5mm [color="Red (633nm)" package="5 mm [THT]"]  # not connected
  R2 = Resistor [tolerance=±5% resistance=220 package=THT]  # not connected
  R3 = Resistor [tolerance=±5% resistance=220 package=THT]
  S1 = Round Pushbutton  # not connected
  R4 = 10k Ω Resistor [package=THT]  # not connected

nets:
  N1: Arduino1.D4, LED1.cathode
  N2: Arduino1.GND, R3.Pin_0
  N3: LED1.anode, R3.Pin_1
